// Logisim project PX16C.circ as structural Verilog: 1 circuit, main circuit main
module main (
);

  wire adder_1_cout, and_1_p3, and_2_out, and_3_p2, and_4_out, and_5_p4, and_6_p3, button_1_out, clock_1_out,
       comparator_1_lt, controlled_buffer_23_out, decoder_1_out0, decoder_1_out1, decoder_1_out2,
       decoder_1_out3, decoder_1_out4, decoder_1_out5, decoder_1_out6, decoder_2_out0, decoder_2_out1,
       decoder_2_out2, decoder_2_out3, decoder_2_out4, decoder_2_out5, decoder_2_out6, decoder_2_out7,
       decoder_3_out0, decoder_3_out1, decoder_3_out2, decoder_3_out3, decoder_3_out4, decoder_3_out5,
       decoder_3_out6, decoder_3_out7, demultiplexer_1_out0, demultiplexer_1_out1, INC, nor_1_p3, not_1_out,
       not_2_out, not_3_out, or_2_out, R4, R6, RM, SCout, Si0, Si1, WM, WR;
  wire [2:0] A, B, D, multiplexer_2_out;
  wire [2:2] or_9_out;
  wire [15:0] Ab, adder_1_out, AR_q, bit_extender_1_out, bit_extender_2_out, bit_extender_3_out,
       controlled_buffer_17_out, controlled_buffer_18_out, Db, imm0_q, imm1_q, or_1_p3, PbA, PbB, PC_q, PF_q,
       R0_q, R1_q, R2_q, R3_q, ram_1_data, Rb, rom_1_data, ST_q, xor_1_out, xor_2_out, xor_3_out, xor_4_out,
       xor_5_out, xor_6_out;

  // Probe on PbA
  DotMatrix #(.inputtype("row"), .matrixcols(8), .matrixrows(2), .dotshape("circle")) dotmatrix_1 (
    .row0(PbA[15:8]), .row1(PbA[7:0]));
  // Probe on PbB
  DotMatrix #(.inputtype("row"), .matrixcols(8), .matrixrows(2), .dotshape("circle")) dotmatrix_2 (
    .row0(PbB[15:8]), .row1(PbB[7:0]));
  // Probe on Rb
  DotMatrix #(.inputtype("row"), .matrixcols(8), .matrixrows(2), .dotshape("circle")) dotmatrix_3 (
    .row0(Rb[15:8]), .row1(Rb[7:0]));
  // Probe on Db
  DotMatrix #(.inputtype("row"), .matrixcols(8), .matrixrows(2), .dotshape("circle")) dotmatrix_4 (
    .row0(Db[15:8]), .row1(Db[7:0]));
  // Probe on Ab
  DotMatrix #(.inputtype("row"), .matrixcols(8), .matrixrows(2), .dotshape("circle")) dotmatrix_5 (
    .row0(Ab[15:8]), .row1(Ab[7:0]));
  // Probe on PbA
  // Probe on PbB
  // Probe on Rb
  // Probe on Db
  // Probe on Ab
  Button button_1 (.out(button_1_out));
  Clock clock_1 (.out(clock_1_out));
  Decoder #(.select(3), .disabled(0), .enable("true")) decoder_1 (
    .out0(decoder_1_out0), .out1(decoder_1_out1), .out2(decoder_1_out2), .out3(decoder_1_out3),
    .out4(decoder_1_out4), .out5(decoder_1_out5), .out6(decoder_1_out6), .out7(WM), .sel(D), .en(WR));
  Register #(.width(16)) R0 (.D(Db), .en(decoder_1_out0), .Q(R0_q), .clk(clock_1_out), .clr(button_1_out));
  Register #(.width(16)) R1 (.D(Db), .en(decoder_1_out1), .Q(R1_q), .clk(clock_1_out), .clr(button_1_out));
  Register #(.width(16)) R2 (.D(Db), .en(decoder_1_out2), .Q(R2_q), .clk(clock_1_out), .clr(button_1_out));
  Register #(.width(16)) R3 (.D(Db), .en(decoder_1_out3), .Q(R3_q), .clk(clock_1_out), .clr(button_1_out));
  Register #(.width(16)) ST (.D(Db), .en(decoder_1_out4), .Q(ST_q), .clk(clock_1_out), .clr(button_1_out));
  Register #(.width(16)) PF (.D(Db), .en(decoder_1_out5), .Q(PF_q), .clk(clock_1_out), .clr(button_1_out));
  Counter #(.width(16), .max('hffff)) PC (
    .load(decoder_1_out6), .D(Db), .count(INC), .Q(PC_q), .clk(clock_1_out), .clr(button_1_out));  // open: carry
  Register #(.width(16)) imm0 (.D(Db), .en(Si0), .Q(imm0_q), .clk(clock_1_out), .clr(button_1_out));
  Register #(.width(16)) imm1 (.D(Db), .en(Si1), .Q(imm1_q), .clk(clock_1_out), .clr(button_1_out));
  assign PbA = decoder_2_out0 ? R0_q : 16'bz;  // Controlled_Buffer controlled_buffer_1
  assign PbB = decoder_3_out0 ? R0_q : 16'bz;  // Controlled_Buffer controlled_buffer_2
  assign PbA = decoder_2_out1 ? R1_q : 16'bz;  // Controlled_Buffer controlled_buffer_3
  assign PbB = decoder_3_out1 ? R1_q : 16'bz;  // Controlled_Buffer controlled_buffer_4
  assign PbA = decoder_2_out2 ? R2_q : 16'bz;  // Controlled_Buffer controlled_buffer_5
  assign PbB = decoder_3_out2 ? R2_q : 16'bz;  // Controlled_Buffer controlled_buffer_6
  assign PbA = decoder_2_out3 ? R3_q : 16'bz;  // Controlled_Buffer controlled_buffer_7
  assign PbB = decoder_3_out3 ? R3_q : 16'bz;  // Controlled_Buffer controlled_buffer_8
  assign PbA = decoder_2_out4 ? ST_q : 16'bz;  // Controlled_Buffer controlled_buffer_9
  assign PbB = decoder_3_out4 ? ST_q : 16'bz;  // Controlled_Buffer controlled_buffer_10
  assign PbA = decoder_2_out5 ? PF_q : 16'bz;  // Controlled_Buffer controlled_buffer_11
  assign PbB = decoder_3_out5 ? PF_q : 16'bz;  // Controlled_Buffer controlled_buffer_12
  assign PbA = decoder_2_out6 ? PC_q : 16'bz;  // Controlled_Buffer controlled_buffer_13
  assign PbB = decoder_3_out6 ? PC_q : 16'bz;  // Controlled_Buffer controlled_buffer_14
  assign PbA = decoder_2_out7 ? imm0_q : 16'bz;  // Controlled_Buffer controlled_buffer_15
  assign PbB = decoder_3_out7 ? imm1_q : 16'bz;  // Controlled_Buffer controlled_buffer_16
  Decoder #(.select(3), .disabled(0)) decoder_2 (
    .out0(decoder_2_out0), .out1(decoder_2_out1), .out2(decoder_2_out2), .out3(decoder_2_out3),
    .out4(decoder_2_out4), .out5(decoder_2_out5), .out6(decoder_2_out6), .out7(decoder_2_out7), .sel(A));  // open: en
  Decoder #(.select(3), .disabled(0)) decoder_3 (
    .out0(decoder_3_out0), .out1(decoder_3_out1), .out2(decoder_3_out2), .out3(decoder_3_out3),
    .out4(decoder_3_out4), .out5(decoder_3_out5), .out6(decoder_3_out6), .out7(decoder_3_out7), .sel(B));  // open: en
  not not_1 (not_1_out, 1'b1);
  assign controlled_buffer_17_out = not_1_out ? PbA : 16'bz;  // Controlled_Buffer controlled_buffer_17
  assign controlled_buffer_18_out = not_2_out ? PbB : 16'bz;  // Controlled_Buffer controlled_buffer_18
  not not_2 (not_2_out, 1'b0);
  // AND_Gate and_1: pin names not known; wires that end beside it: 1'b0, 1'b0, and_1_p3, 1'b0, 1'b0
  Register #(.width(16)) AR (.D(Rb), .en(1'b1), .Q(AR_q), .clk(clock_1_out), .clr(button_1_out));
  ExactlyOne xor_1[15:0] (
    .out(xor_1_out), .in1(controlled_buffer_17_out), .in3(bit_extender_1_out), .in4(controlled_buffer_18_out));
  assign controlled_buffer_17_out = 1'b1 ? {16{1'b0}} : 16'bz;  // Controlled_Buffer controlled_buffer_19
  assign controlled_buffer_18_out = 1'b0 ? {16{1'b0}} : 16'bz;  // Controlled_Buffer controlled_buffer_20
  ExactlyOne xor_2[15:0] (
    .out(xor_2_out), .in0(bit_extender_1_out), .in1(controlled_buffer_18_out), .in3(bit_extender_2_out));
  assign bit_extender_1_out = {{15{1'b0}}, 1'b0};  // Bit_Extender bit_extender_1
  assign bit_extender_2_out = {{15{1'b0}}, 1'b0};  // Bit_Extender bit_extender_2
  assign bit_extender_3_out = {{15{and_1_p3}}, and_1_p3};  // Bit_Extender bit_extender_3
  Multiplexer #(.width(16)) multiplexer_1 (.in0(Rb), .in1(AR_q), .out(Ab), .sel(WM));  // open: en
  not not_3 (not_3_out, RM);
  assign Db = not_3_out ? Rb : 16'bz;  // Controlled_Buffer controlled_buffer_21
  Adder #(.width(16)) adder_1 (.a(xor_1_out), .b(xor_2_out), .out(adder_1_out), .cin(1'b0), .cout(adder_1_cout));
  ExactlyOne xor_3[15:0] (.out(xor_3_out), .in1(xor_1_out), .in3(16'h8000), .in4(xor_2_out));
  Adder #(.width(16)) adder_2 (.a(xor_3_out), .b(xor_4_out), .cout(SCout));  // open: out, cin
  ExactlyOne xor_4[15:0] (.out(xor_4_out), .in0(16'h8000), .in1(xor_2_out), .in3(16'h8000));
  assign xor_5_out = xor_1_out ^ xor_2_out;  // XOR_Gate xor_5, 16 bits wide
  // OR_Gate #(.width(16)) or_1: pin names not known; wires that end beside it: xor_1_out, xor_2_out, or_1_p3
  assign xor_6_out = or_1_p3 ^ bit_extender_3_out;  // XOR_Gate xor_6, 16 bits wide
  ROM #(.addrWidth(16), .dataWidth(16)) rom_1 (.addr(Ab), .data(rom_1_data), .sel(1'b1));
  RAM #(.addrWidth(16), .dataWidth(16)) ram_1 (
    .addr(Ab), .data(ram_1_data), .sel(1'b1), .clk(clock_1_out), .ld(WM), .clr(button_1_out));
  Comparator #(.width(16), .mode("unsigned")) comparator_1 (
    .a(Ab), .b({16{1'b1}}), .lt(comparator_1_lt));  // open: gt, eq
  assign Rb = 1'b1 ? adder_1_out : 16'bz;  // Controlled_Buffer controlled_buffer_22
  assign controlled_buffer_23_out = 1'b1 ? adder_1_cout : 1'bz;  // Controlled_Buffer controlled_buffer_23
  Pull_Resistor pull_resistor_1 (.node(controlled_buffer_23_out));
  assign Rb = 1'b0 ? xor_5_out : 16'bz;  // Controlled_Buffer controlled_buffer_24
  assign Rb = 1'b0 ? xor_6_out : 16'bz;  // Controlled_Buffer controlled_buffer_25
  assign Rb = 1'b0 ? {xor_1_out[14:0], 1'b0} : 16'bz;  // Controlled_Buffer controlled_buffer_26
  assign controlled_buffer_23_out = 1'b0 ? xor_1_out[15] : 1'bz;  // Controlled_Buffer controlled_buffer_27
  assign Rb = 1'b0 ? {1'b0, xor_1_out[15:1]} : 16'bz;  // Controlled_Buffer controlled_buffer_28
  assign controlled_buffer_23_out = 1'b0 ? xor_1_out[0] : 1'bz;  // Controlled_Buffer controlled_buffer_29
  assign Db = and_2_out ? rom_1_data : 16'bz;  // Controlled_Buffer controlled_buffer_30
  assign ram_1_data = WM ? Db : 16'bz;  // Controlled_Buffer controlled_buffer_31
  assign Db = and_3_p2 ? ram_1_data : 16'bz;  // Controlled_Buffer controlled_buffer_32
  and and_2 (and_2_out, RM, comparator_1_lt, RM);
  // AND_Gate and_3: pin names not known; wires that end beside it: comparator_1_lt, and_3_p2
  or or_2 (or_2_out, 1'b0, 1'b0, 1'b0);
  // OR_Gate or_3: pin names not known; wires that end beside it: 1'b0, 1'b0, 1'b0, INC
  and and_4 (and_4_out, 1'b1, nor_1_p3);
  Demultiplexer #(.disabled(0)) demultiplexer_1 (
    .out0(demultiplexer_1_out0), .out1(demultiplexer_1_out1), .in(and_4_out), .sel(1'b0));  // open: en
  // NOR_Gate nor_1: pin names not known; wires that end beside it: 1'b0, 1'b0, nor_1_p3
  // AND_Gate and_5: pin names not known; wires that end beside it: 1'b1, 1'b0, 1'b0, and_5_p4
  // AND_Gate and_6: pin names not known; wires that end beside it: 1'b0, 1'b0, and_6_p3
  or or_4 (R6, or_2_out, INC);
  // OR_Gate or_5: pin names not known; wires that end beside it: 1'b0, demultiplexer_1_out0, Si0
  or or_6 (R4, 1'b0, 1'b0, 1'b0);
  or or_7 (RM, INC, or_2_out, 1'b0);
  or or_8 (WR, and_5_p4, and_6_p3);
  or or_9 (or_9_out[2], R6, R4);
  Multiplexer #(.width(3), .disabled(0)) multiplexer_2 (
    .in0(3'b101), .in1(3'b011), .out(multiplexer_2_out), .sel(1'b0));  // open: en
  // OR_Gate or_10: pin names not known; wires that end beside it: 1'b0, demultiplexer_1_out1, Si1
  assign A = or_9_out[2] ? {or_9_out[2], R6, 1'b0} : 3'bz;  // Controlled_Buffer controlled_buffer_33
  assign A = 1'b1 ? 3'b010 : 3'bz;  // Controlled_Buffer controlled_buffer_34
  Pull_Resistor pull_resistor_2 (.node(A));
  assign A = 1'b0 ? 3'b011 : 3'bz;  // Controlled_Buffer controlled_buffer_35
  assign B = or_9_out[2] ? {or_9_out[2], R6, 1'b0} : 3'bz;  // Controlled_Buffer controlled_buffer_36
  Pull_Resistor pull_resistor_3 (.node(B));
  assign B = 1'b1 ? multiplexer_2_out : 3'bz;  // Controlled_Buffer controlled_buffer_37
  assign B = 1'b0 ? 3'b101 : 3'bz;  // Controlled_Buffer controlled_buffer_38
  assign D = or_9_out[2] ? {or_9_out[2], R6, 1'b0} : 3'bz;  // Controlled_Buffer controlled_buffer_39
  assign D = 1'b1 ? 3'b011 : 3'bz;  // Controlled_Buffer controlled_buffer_40
  Pull_Resistor pull_resistor_4 (.node(D));
  assign D = 1'b0 ? 3'b011 : 3'bz;  // Controlled_Buffer controlled_buffer_41

  // Notes on the sheet:
  //   PbA
  //   PbB
  //   Rb
  //   Db
  //   Ab
  //   regfile
  //   ALU
  //   MEM
  //   SHL
  //   SHR
  //   contents of rom_1 (hex, n*v repeats v):
  //   0 0 cccc 52425*0 ffee
  //   CU
  //   Boot 0
  //   Boot 1
  //   Load 0
  //   Load 1
  //   Load 2
  //   Push
  //   Jsr
  //   Pop
  //   Addr
  //   Act
  //   MOV
  //   LEA
  //   ARx
  //   AMM
  //   IMM
  //   ACT
  //   CMP
  //   ADD
  //   SUB
  //   AND
  //   OR
  //   XOR
  //   SHL
  //   SHR
endmodule
